# Fritzing sketch capture_point (saved by Fritzing 0.9.3b)

parts:
  Часть1 = Arduino Nano (Rev3.0)
  S1 = Pushbutton [package="[THT]"]
  S2 = Pushbutton [package="[THT]"]
  J1 = Piezo Speaker
  LCD1 = LCD screen  # not connected
  VCC1 = Battery block 9V

nets:
  N1: Часть1.D6, S1.Pin_1, S1.Pin_2
  N2: Часть1.D7, S2.Pin_1, S2.Pin_2
  N3: Часть1.D9, J1.pin2
  N4: Часть1.VIN, VCC1.+
  N5: Часть1.GND, S1.Pin_3, S1.Pin_4, S2.Pin_3, J1.pin1, VCC1.-
